# Fritzing sketch scheme (saved by Fritzing 0.9.4)
circuit board: 8.46667cm x 5.64444cm
breadboards: 1

parts:
  Компонент1 = Arduino Nano (Rev3.0)
  microSD1 = MicroSD Card Module
  Компонент2 = Barometric Pressure Sensor - BMP180 Breakout (GY-68)
  Компонент3 = InvenSense MPU6050

nets:
  GND: Компонент1.GND, microSD1.GND, Компонент2.GND
  N1: Компонент1.D2, Компонент3.GND
  N2: Компонент1.D5, microSD1.CS
  N3: Компонент1.D11/MOSI, microSD1.MOSI
  N4: Компонент1.D12/MISO, microSD1.MISO
  5V: Компонент1.5V, Компонент3.VCC
  N5: Компонент1.A5, Компонент2.SCL, Компонент3.SCL
  N6: Компонент1.A4, Компонент2.SDA, Компонент3.SDA
  VCC: Компонент1.3V3, microSD1.VCC, Компонент2.VCC
  N7: Компонент1.D13/SCK, microSD1.SCK
